# Fritzing sketch Antifurto (saved by Fritzing 0.7.4b)
breadboards: 1

parts:
  Arduino1 = Arduino
  J2 = Infrared Proximity Sensor
  J3 = Infrared Proximity Sensor

nets:
  VCC: Arduino1.+5V, J2.Vcc, J3.Vcc
  GND: Arduino1.GND, J2.GND, J3.GND
